# Fritzing sketch Turn an LED on and off (saved by Fritzing 0.9.2b)
breadboards: 1

parts:
  LED1 = smd LED [color="Red (633nm)" package="0603 [SMD]"]
  Part1 = Arduino Uno (Rev3)
  R1 = Resistor [tolerance=±5% resistance=220 package=THT]

nets:
  N1: LED1.cathode, Part1.GND
  N2: LED1.anode, R1.Pin_0
  N3: Part1.D13/SCK, R1.Pin_1
